// Logisim project ControlUnit.circ as structural Verilog: 1 circuit, main circuit ControlUnit
module ControlUnit (
  input  [5:0] Opcode,
  input  [5:0] Func,
  output ALUSrc,
  output ALUOp,
  output RegWrite,
  output MemWrite,
  output JAL,
  output JumpReg,
  output RegDest,
  output Jump,
  output Branch,
  output MemRead,
  output MemToReg
);

  wire and_3_out, and_4_out, and_5_out, and_6_out, and_7_out, fu0not, fu1not, fu2not, fu3not, fu4not, fu5not,
       op0not, op1not, op2not, op3not, op4not, op5not, or_1_out, or_2_out, or_3_out;

  not not_1 (op0not, Opcode[0]);
  not not_2 (fu0not, Func[0]);
  not not_3 (op1not, Opcode[1]);
  not not_4 (op2not, Opcode[2]);
  not not_5 (op3not, Opcode[3]);
  not not_6 (op4not, Opcode[4]);
  not not_7 (op5not, Opcode[5]);
  not not_8 (fu1not, Func[1]);
  not not_9 (fu2not, Func[2]);
  not not_10 (fu3not, Func[3]);
  not not_11 (fu4not, Func[4]);
  not not_12 (fu5not, Func[5]);
  and and_1 (JAL, op0not, op1not, op2not, op3not, Opcode[4], Opcode[5]);
  and and_2 (JumpReg, op0not, op1not, Opcode[2], op3not, op4not, op5not);
  nor nor_1 (RegDest, Opcode[0], Opcode[1], Opcode[2], Opcode[3], Opcode[4], Opcode[5]);
  not not_13 (ALUSrc, RegDest);
  and and_3 (and_3_out, Opcode[4], Opcode[5]);
  and and_4 (and_4_out, op4not, op5not);
  and and_5 (and_5_out, Opcode[2], op4not, op5not);
  and and_6 (and_6_out, op2not, Opcode[4]);
  and and_7 (and_7_out, op3not, op4not, Opcode[5]);
  or or_1 (or_1_out, and_3_out, and_4_out);
  or or_2 (or_2_out, and_5_out, and_6_out);
  or or_3 (or_3_out, Opcode[3], and_7_out);
  and and_8 (MemRead, Opcode[0], op1not, op3not, op2not, or_1_out);
  and and_9 (MemWrite, or_1_out, Opcode[0], op1not, Opcode[2], op3not);
  and and_10 (Jump, op0not, op1not, op3not, or_2_out);
  and and_11 (Branch, op0not, op1not, op2not, or_3_out);

  assign MemToReg = MemRead;

  // Other names for the same wires on the sheet: fu0 = Func[0]; fu1 = Func[1]; fu2 = Func[2]; fu3 = Func[3];
  //   fu4 = Func[4]; fu5 = Func[5]; op0 = Opcode[0]; op1 = Opcode[1]; op2 = Opcode[2]; op3 = Opcode[3];
  //   op4 = Opcode[4]; op5 = Opcode[5]

  // Notes on the sheet:
  //   Control Unit inputs
  //   Control Unit outputs
endmodule
