// Logisim project EX_MEM_buffer.circ as structural Verilog: 1 circuit, main circuit EX_MEM
module EX_MEM (
  input  clk,
  input  [31:0] Result,
  input  [31:0] RD2,
  input  [4:0] Write,
  input  Zero,
  input  Branch,
  input  [3:0] MemMask,
  input  MemToReg,
  input  JAL,
  input  RegWrite,
  output [31:0] n_Result,
  output [31:0] n_RD2,
  output [4:0] n_Write,
  output n_Zero,
  output n_Branch,
  output [3:0] n_MemMask,
  output n_MemToReg,
  output n_JAL,
  output n_RegWrite
);

  Register #(.width(32)) register_1 (.D(Result), .en(1'b1), .clk(clk), .Q(n_Result));  // open: clr
  Register #(.width(32)) register_2 (.D(RD2), .en(1'b1), .clk(clk), .Q(n_RD2));  // open: clr
  Register #(.width(1)) register_3 (.D(Zero), .en(1'b1), .clk(clk), .Q(n_Zero));  // open: clr
  Register #(.width(5)) register_4 (.D(Write), .en(1'b1), .clk(clk), .Q(n_Write));  // open: clr
  Register #(.width(1)) register_5 (.D(Branch), .en(1'b1), .clk(clk), .Q(n_Branch));  // open: clr
  Register #(.width(1)) register_6 (.D(MemToReg), .en(1'b1), .clk(clk), .Q(n_MemToReg));  // open: clr
  Register #(.width(1)) register_7 (.D(JAL), .en(1'b1), .clk(clk), .Q(n_JAL));  // open: clr
  Register #(.width(4)) register_8 (.D(MemMask), .en(1'b1), .clk(clk), .Q(n_MemMask));  // open: clr
  Register #(.width(1)) register_9 (.D(RegWrite), .en(1'b1), .clk(clk), .Q(n_RegWrite));  // open: clr

  // Notes on the sheet:
  //   inputs
  //   outputs
endmodule
