// Logisim project MEM_WB_buffer.circ as structural Verilog: 1 circuit, main circuit MEM_WB
module MEM_WB (
  input  clk,
  input  [31:0] Result,
  input  [31:0] Data,
  input  [4:0] Write,
  output [31:0] n_Result,
  output [31:0] n_Data,
  output [4:0] n_Write
);

  Register #(.width(32)) register_1 (.D(Result), .en(1'b1), .clk(clk), .Q(n_Result));  // open: clr
  Register #(.width(32)) register_2 (.D(Data), .en(1'b1), .clk(clk), .Q(n_Data));  // open: clr
  Register #(.width(5)) register_3 (.D(Write), .en(1'b1), .clk(clk), .Q(n_Write));  // open: clr

  // Notes on the sheet:
  //   inputs
  //   outputs
endmodule
