// Logisim project MemAddressGen.circ as structural Verilog: 1 circuit, main circuit MemAddressGen
module MemAddressGen (
  input  [13:0] address,
  input  miss,
  input  clk,
  input  read,
  output [3:0] memmask,
  output [13:0] memaddress,
  output readmem
);

  wire and_1_out, and_2_out, not_1_out, not_2_out, or_1_out, t_ff_1_qn;

  and and_1 (and_1_out, 1'b0, t_ff_1_qn);
  not not_1 (not_1_out, 1'b0);
  T_Flip_Flop t_ff_1 (.T(not_1_out), .clk(clk), .Q(memaddress[0]), .Qn(t_ff_1_qn), .reset(not_2_out));  // open: preset
  and and_2 (and_2_out, not_1_out, memaddress[0]);
  or or_1 (or_1_out, and_2_out, and_1_out);
  T_Flip_Flop t_ff_2 (.T(or_1_out), .clk(clk), .Q(memaddress[1]), .reset(not_2_out));  // open: Qn, preset
  not not_2 (not_2_out, miss);

  assign memaddress[13:2] = address[13:2];
  assign memmask = 4'b1111;
  assign readmem = read;

  // Other names for the same wires on the sheet: bit0 = memaddress[0]; bit1 = memaddress[1];
  //   address_t[11:0] = address[13:2]

  // Notes on the sheet:
  //   Inputs
  //   output
endmodule
