// Logisim project cpu.circ as structural Verilog: 1 circuit, main circuit cpu
module cpu (
  input  in_1,
  input  in_2,
  input  [3:0] in_3,
  input  [31:0] in_4,
  input  in_5
);

  wire ALUOpValid, ALUSrc, and_3_out, and_4_out, and_5_out, and_6_out, and_7_out, and_8_out, Branch,
       cacheClk, cacheWrite, clk, comparator_1_eq, comparator_2_eq, CPUclk, En1, En2, is_op, JAL, Jump,
       JumpReg, LB, MemToReg, memWrite, miss, multiplexer_2_out, multiplexer_4_out, not_1_out, not_2_out,
       not_3_out, not_4_out, not_5_out, not_6_out, not_7_out, not_8_out, not_9_out, not_10_out, not_11_out,
       not_12_out, not_13_out, not_14_out, not_15_out, or_2_out, RegDes, RegWrite, SLTi, syscall, validMiss,
       zero;
  wire [3:0] counter_1_q, counter_2_q, MemMask, memtocache_1_memmask;
  wire [4:0] instr2, instr3, multiplexer_3_out, multiplexer_5_out;
  wire [5:0] ALUOp, func, opcd_fnc, opcode;
  wire [13:0] cache_1_address_out;
  wire [15:2] MemAddr;
  wire [15:6] instr0;
  wire [31:0] adder_1_out, adder_2_out, extended, final_writeData, MemData, memData_t, memtocache_1_word,
       memWriteData, multiplexer_6_out, multiplexer_8_out, multiplexer_10_out, new_PC, PC, rdData2,
       RegisterFile_p7, result, shifter_1_out, W0, w0_t, W1, w1_t, W2, w2_t, W3, w3_t, writeData;

  not not_1 (not_1_out, syscall);
  Register #(.width(32)) register_1 (.D(new_PC), .en(not_1_out), .clk(CPUclk), .Q(PC), .clr(in_2));
  not not_2 (not_2_out, validMiss);
  Adder #(.width(32)) adder_1 (.a(PC), .b(32'h4), .out(adder_1_out), .cin(1'b0));  // open: cout
  Clock clock_1 (.out(clk));
  and and_1 (En1, miss, validMiss);
  and and_2 (En2, miss, not_2_out);
  Counter #(.max('hf), .width(4)) counter_1 (
    .load(comparator_2_eq), .D(4'b0000), .count(En2), .Q(counter_1_q), .up(1'b1), .clk(clk));  // open: carry, clr
  Counter #(.max('hf), .width(4)) counter_2 (
    .D(4'b0000), .count(En1), .Q(counter_2_q), .up(1'b1), .clk(clk), .clr(comparator_1_eq));  // open: load, carry
  not not_3 (not_3_out, counter_2_q[1]);
  Comparator #(.width(4)) comparator_1 (.a(counter_2_q), .b(4'b1101), .eq(comparator_1_eq));  // open: gt, lt
  Comparator #(.width(4)) comparator_2 (.a(counter_1_q), .b(4'b1000), .eq(comparator_2_eq));  // open: gt, lt
  not not_4 (not_4_out, counter_1_q[0]);
  not not_5 (not_5_out, counter_1_q[1]);
  not not_6 (not_6_out, counter_1_q[2]);
  // mem mem_1: pin names not known; wires that end beside it: PC, in_3, in_4, CPUclk, {opcode, instr3, instr2, instr0, func}
  and and_3 (and_3_out, not_4_out, not_5_out, clk, not_6_out, counter_1_q[3]);
  and and_4 (and_4_out, counter_2_q[0], not_3_out, counter_2_q[2], counter_2_q[3], clk);
  Multiplexer #(.width(32)) multiplexer_1 (
    .in0(writeData), .in1({rdData2[31:8], writeData[7:0]}), .out(final_writeData), .sel(LB));
  Multiplexer multiplexer_2 (.in0(and_3_out), .in1(and_4_out), .out(multiplexer_2_out), .sel(validMiss));
  Shifter #(.width(32)) shifter_1 (.in(extended), .\dist (5'b00010), .out(shifter_1_out));
  Multiplexer #(.width(5)) multiplexer_3 (.in0(instr2), .in1(instr0[15:11]), .out(multiplexer_3_out), .sel(RegDes));
  Multiplexer multiplexer_4 (.in0(clk), .in1(multiplexer_2_out), .out(multiplexer_4_out), .sel(miss));
  Adder #(.width(32)) adder_2 (.a(adder_1_out), .b(shifter_1_out), .out(adder_2_out), .cin(1'b0));  // open: cout
  Multiplexer #(.width(5)) multiplexer_5 (.in0(multiplexer_3_out), .in1({5{1'b1}}), .out(multiplexer_5_out), .sel(JAL));
  Multiplexer #(.width(32)) multiplexer_6 (.in0(final_writeData), .in1(PC), .out(multiplexer_6_out), .sel(JAL));
  Multiplexer multiplexer_7 (.in0(multiplexer_4_out), .in1(clk), .out(CPUclk), .sel(in_5));
  Multiplexer #(.width(32)) multiplexer_8 (
    .in0(adder_1_out), .in1(adder_2_out), .out(multiplexer_8_out), .sel(and_5_out));
  and and_5 (and_5_out, zero, Branch);
  Multiplexer #(.width(32)) multiplexer_9 (
    .in0(multiplexer_8_out), .in1({PC[31:28], instr3, instr2, instr0, func, 2'b00}), .out(new_PC), .sel(Jump));
  SignExtend signextend_1 (.inpt({instr0, func}), .opcode(opcode), .outpt(extended));
  // regfile RegisterFile: pin names not known; wires that end beside it: instr3, instr2, multiplexer_6_out, RegWrite, CPUclk, multiplexer_5_out, RegisterFile_p7, rdData2
  Multiplexer #(.width(32)) multiplexer_10 (.in0(rdData2), .in1(extended), .out(multiplexer_10_out), .sel(ALUSrc));
  // ControlUnit controlunit_1: pin names not known; wires that end beside it: opcode, func, ALUSrc, RegWrite, ALUOp, ALUOpValid, MemMask, JAL, JumpReg, RegDes, Jump, Branch, LB, MemToReg, syscall, SLTi
  aluControl alucontrol_1 (.func(func), .aluOP(ALUOp), .opcd_fnc(opcd_fnc), .is_op(is_op));
  alu alu_1 (
    .rs(RegisterFile_p7), .rt_imm(multiplexer_10_out), .opcd_fnc(opcd_fnc), .shft_amt(instr0[10:6]),
    .is_i(is_op), .result(result), .zero(zero));
  Multiplexer #(.width(32)) multiplexer_11 (.in0(result), .in1(MemData), .out(writeData), .sel(MemToReg));
  not not_7 (not_7_out, MemMask[0]);
  not not_8 (not_8_out, MemMask[1]);
  not not_9 (not_9_out, MemMask[2]);
  and and_6 (and_6_out, not_7_out, not_8_out, not_9_out, MemMask[3]);
  Multiplexer #(.width(32)) multiplexer_12 (
    .in0(rdData2), .in1({MemData[31:8], rdData2[7:0]}), .out(memWriteData), .sel(and_6_out));
  Multiplexer #(.width(32)) multiplexer_13 (.in0(w0_t), .in1(memData_t), .out(W0), .sel(not_10_out));
  Multiplexer #(.width(32)) multiplexer_14 (.in0(w1_t), .in1(memData_t), .out(W1), .sel(not_10_out));
  Multiplexer #(.width(32)) multiplexer_15 (.in0(w2_t), .in1(memData_t), .out(W2), .sel(not_10_out));
  Multiplexer #(.width(32)) multiplexer_16 (.in0(w3_t), .in1(memData_t), .out(W3), .sel(not_10_out));
  cache cache_1 (
    .address(result[15:2]), .reset(in_1), .clock(cacheClk), .write(cacheWrite), .data_in(memWriteData),
    .data_out(MemData), .valid_miss(miss), .miss(validMiss), .w0_out(w0_t), .w1_out(w1_t),
    .address_out(cache_1_address_out), .w2_out(w2_t), .w3_out(w3_t));  // open: hit
  not not_10 (not_10_out, memWrite);
  memToCache memtocache_1 (
    .miss(validMiss), .validmiss(miss), .word_0(W0), .word_1(W1), .word_2(W2), .word_3(W3),
    .address_out(cache_1_address_out), .clk(cacheClk), .memmask(memtocache_1_memmask), .memwrite(memWrite),
    .word(memtocache_1_word), .address(MemAddr));
  // memDelayed memdelayed_1: pin names not known; wires that end beside it: {{16{1'b0}}, MemAddr, 2'b00}, memtocache_1_memmask, memtocache_1_word, cacheClk, memData_t
  not not_11 (not_11_out, opcode[2]);
  not not_12 (not_12_out, opcode[4]);
  and and_7 (and_7_out, opcode[0], opcode[1], not_11_out, opcode[3], not_12_out, opcode[5]);
  not not_13 (not_13_out, opcode[2]);
  not not_14 (not_14_out, opcode[3]);
  not not_15 (not_15_out, opcode[4]);
  or or_1 (cacheWrite, and_7_out, memWrite);
  and and_8 (and_8_out, opcode[0], opcode[1], not_13_out, not_14_out, not_15_out, opcode[5]);
  or or_2 (or_2_out, and_7_out, and_8_out);
  and and_9 (cacheClk, or_2_out, clk);

  // Other names for the same wires on the sheet: instr0[5:0] = func; Jinstr[25:0] = {instr3, instr2, instr0, func};
  //   sh_amount[4:0] = instr0[10:6]; instr1[4:0] = instr0[15:11]; MemToCacheAddr[13:0] = MemAddr
endmodule
