// Logisim project memToCache.circ as structural Verilog: 1 circuit, main circuit memToCache
module memToCache (
  input  miss,
  input  validmiss,
  input  [31:0] word_0,
  input  [31:0] word_1,
  input  [31:0] word_2,
  input  [31:0] word_3,
  input  [13:0] address_out,
  input  clk,
  output [3:0] memmask,
  output memwrite,
  output [31:0] word,
  output [13:0] address
);

  wire miss_t;

  and and_1 (miss_t, miss, validmiss);
  MemAddressGen memaddressgen_1 (
    .address(address_out), .miss(miss_t), .clk(clk), .read(miss_t), .memmask(memmask), .memaddress(address));  // open: readmem
endmodule
