// Logisim project sign_extend.circ as structural Verilog: 1 circuit, main circuit SignExtend
module SignExtend (
  input  [15:0] inpt,
  input  [5:0] opcode,
  output [31:0] outpt
);


  assign outpt = {{17{inpt[15]}}, inpt[14:0]};

  // Notes on the sheet:
  //   16 bit input
  //   extender
  //   32-bit output
endmodule
